// Logisim project 8bit_ALU.circ as structural Verilog: 3 circuits, main circuit main
module main (
  input  [7:0] in_1,
  input  [7:0] in_2,
  output [7:0] out_3
);

  CPU_ALU_8BIT_ADDER cpu_alu_8bit_adder_1 (.out_3(out_3), .A(in_1), .B(in_2));
endmodule

module CPU_ALU_1BIT_ADDER (
  input  A,
  input  B,
  input  Cin,
  output OUT,
  output Cout
);

  wire and_1_out, and_2_out, xor_1_out;

  and and_1 (and_1_out, A, B);
  xor xor_1 (xor_1_out, A, B);
  and and_2 (and_2_out, xor_1_out, Cin);
  or or_1 (Cout, and_1_out, and_2_out);
  xor xor_2 (OUT, xor_1_out, Cin);
endmodule

module CPU_ALU_8BIT_ADDER (
  input  [7:0] A,
  input  [7:0] B,
  output [7:0] out_3
);

  wire cpu_alu_1bit_adder_1_cout, cpu_alu_1bit_adder_2_cout, cpu_alu_1bit_adder_3_cout,
       cpu_alu_1bit_adder_4_cout, cpu_alu_1bit_adder_5_cout, cpu_alu_1bit_adder_6_cout,
       cpu_alu_1bit_adder_7_cout;

  CPU_ALU_1BIT_ADDER cpu_alu_1bit_adder_1 (
    .A(A[0]), .B(B[0]), .Cin(1'b0), .OUT(out_3[0]), .Cout(cpu_alu_1bit_adder_1_cout));
  CPU_ALU_1BIT_ADDER cpu_alu_1bit_adder_2 (
    .A(A[1]), .B(B[1]), .Cin(cpu_alu_1bit_adder_1_cout), .OUT(out_3[1]), .Cout(cpu_alu_1bit_adder_2_cout));
  CPU_ALU_1BIT_ADDER cpu_alu_1bit_adder_3 (
    .A(A[2]), .B(B[2]), .Cin(cpu_alu_1bit_adder_2_cout), .OUT(out_3[2]), .Cout(cpu_alu_1bit_adder_3_cout));
  CPU_ALU_1BIT_ADDER cpu_alu_1bit_adder_4 (
    .A(A[3]), .B(B[3]), .Cin(cpu_alu_1bit_adder_3_cout), .OUT(out_3[3]), .Cout(cpu_alu_1bit_adder_4_cout));
  CPU_ALU_1BIT_ADDER cpu_alu_1bit_adder_5 (
    .A(A[4]), .B(B[4]), .Cin(cpu_alu_1bit_adder_4_cout), .OUT(out_3[4]), .Cout(cpu_alu_1bit_adder_5_cout));
  CPU_ALU_1BIT_ADDER cpu_alu_1bit_adder_6 (
    .A(A[5]), .B(B[5]), .Cin(cpu_alu_1bit_adder_5_cout), .OUT(out_3[5]), .Cout(cpu_alu_1bit_adder_6_cout));
  CPU_ALU_1BIT_ADDER cpu_alu_1bit_adder_7 (
    .A(A[6]), .B(B[6]), .Cin(cpu_alu_1bit_adder_6_cout), .OUT(out_3[6]), .Cout(cpu_alu_1bit_adder_7_cout));
  CPU_ALU_1BIT_ADDER cpu_alu_1bit_adder_8 (
    .A(A[7]), .B(B[7]), .Cin(cpu_alu_1bit_adder_7_cout), .OUT(out_3[7]));  // open: Cout
endmodule
